# Fritzing sketch Action Module circuit v1 (saved by Fritzing 1.0.1rc)
breadboards: 1

parts:
  Componente1 = Arduino Uno (Rev3)
  J1 = Basic Servo
  J2 = Basic Servo
  Componente3 = Thumb Joystick
  Raspberry_Pi1 = Raspberry Pi B+  # not connected

nets:
  N1: Componente1.A0, Componente3.VERT
  N2: Componente1.A1, Componente3.HORZ
  N3: Componente1.D2, Componente3.SEL
  N4: Componente1.D5_PWM, J2.pulse
  N5: Componente1.D6_PWM, J1.pulse
  VCC: Componente1.5V, J1.vcc, J2.vcc, Componente3.VCC
  GND: Componente1.GND, J1.gnd, J2.gnd, Componente3.GND

// code stored in the sketch: codigo.ino
#include <Servo.h>

Servo servoExterior;
Servo servoInterior;

void setup(){
	//Enlazamos el motor exterior al pin 5
	servoExterior.attach(5);

	//Enlazamos el motor interior al pin 6
	servoInterior.attach(6);
}

void loop(){
	//Desplazar motor exterior a 0º
	servoExterior.write(0);
	
	//Esperar 1 segundo (esta en milisegundos)
	delay(1000);

	//Desplazar a 90º
	servoExterior.write(90);
}
